# Fritzing sketch SmarTo_diagram (saved by Fritzing 0.9.3b)

parts:
  Raspberry_Pi1 = Raspberry Pi B+
  Componente1 = Ambient Light Sensor (TEMT6000 Breakout Board)
  R1 = Photocell (LDR) [package=THT]  # not connected
  PIR2 = PIR sensor

nets:
  N1: Raspberry_Pi1.GPIO4, PIR2.SIG
  GND: Raspberry_Pi1.GND, Componente1.GND, PIR2.GND
  N2: Raspberry_Pi1.GPIO17, Componente1.S
  5V: Raspberry_Pi1.5V, Componente1.VCC, PIR2.VDD
